# Fritzing sketch all (saved by Fritzing 0.9.3b)
breadboards: 1

parts:
  Voltage_Regulator_5v = Voltage Regulator [package=to220-igo]
  IC5 = L293D [package=THT]
  VCC = Battery block 9V
  R11 = Resistor [tolerance=±5% resistance=10k package=THT]
  U3 = atmega328 [package=dip]
  Motor_Wheel_3 = male pin header, 2 pins [form="♂ (male)"]
  Motor_Wheel_4 = male pin header, 2 pins [form="♂ (male)"]
  BlueTooth_(HC05) = Bluetooth HC-05 Macho
  C9 = Electrolytic Capacitor [capacitance=10μF voltage=50V package="0605 [SMD, electrolytic]"]
  C10 = Electrolytic Capacitor [capacitance=10μF voltage=50V package="0605 [SMD, electrolytic]"]
  XTAL2 = Crystal [frequency="16 Mhz" package=THT]
  C11 = Ceramic Capacitor [capacitance=22pF voltage=16V package="100 mil [THT, multilayer]"]
  C12 = Ceramic Capacitor [capacitance=22pF voltage=16V package="100 mil [THT, multilayer]"]
  D4 = Rectifier Diode [part_number=1N4001 package="300 mil [THT]"]
  D5 = Rectifier Diode [part_number=1N4001 package="300 mil [THT]"]
  R12 = Resistor [tolerance=±5% resistance=1k package=THT]
  R13 = Resistor [tolerance=±5% resistance=1.8k package=THT]
  R14 = Resistor [tolerance=±5% resistance=220 package="0402 [SMD]"]
  LED1 = smd LED [color="Green (570nm)" package="1206 [SMD]"]
  Switch = SPST Switch [package=switch-spdt-smd]

nets:
  GND: Voltage_Regulator_5v.GND, IC5.0V, VCC.-, U3.GND, BlueTooth_(HC05).GND, C9.-, C10.-, C11.1, C12.1, R12.Pin_1, LED1.cathode
  N1: Voltage_Regulator_5v.IN, C10.+, Switch.S
  N2: Voltage_Regulator_5v.OUT, C9.+, D5.anode, R14.Pin_0
  VCC: IC5.Enable_1, IC5.Enable_2, IC5.+V, R11.Pin_0, U3.VCC, U3.AVCC, U3.AREF, BlueTooth_(HC05).VCC, D5.cathode
  N3: IC5.In_1, U3.D9_(PWM)
  N4: IC5.Out_1_(_Controlled_by_Enable_1_), Motor_Wheel_4.pin1
  N5: IC5.Out_2_(_Controlled_by_Enable_1_), Motor_Wheel_4.pin2
  N6: IC5.In_2, U3.D10_(PWM)
  N7: IC5.+Vmotor, D4.cathode
  N8: IC5.In_3, U3.D6_(PWM)
  N9: IC5.Out_3_(_Controlled_by_Enable_2_), Motor_Wheel_3.pin2
  N10: IC5.Out_4_(_Controlled_by_Enable_2_), Motor_Wheel_3.pin1
  N11: IC5.In_4, U3.D5_(PWM)
  N12: VCC.+, D4.anode, Switch.P
  N13: R11.Pin_1, U3.RESET
  N14: U3.D0_(RX), BlueTooth_(HC05).RXD
  N15: U3.D1_(TX), R13.Pin_0
  N16: U3.XLAT1, XTAL2.pin_1, C12.0
  N17: U3.XLAT2, XTAL2.pin_0, C11.0
  N18: BlueTooth_(HC05).TXD, R12.Pin_0
  N19: R14.Pin_1, LED1.anode
