# Fritzing sketch arduino (saved by Fritzing 0.9.3b)
breadboards: 1

parts:
  VDC_IN = DC Power [voltage=5V]
  R9 = Resistor [tolerance=±5% resistance=1k package=THT]
  R10 = Resistor [tolerance=±5% resistance=1.8k package=THT]
  R11 = Resistor [tolerance=±5% resistance=10k package=THT]
  U3 = atmega328 [package=dip]
  Motor_Wheel_Signal_3 = male pin header, 2 pins [form="♂ (male)"]
  Motor_Wheel_Signal_4 = male pin header, 2 pins [form="♂ (male)"]
  BlueTooth_HC6 = rounded female pin header, 6 pins [form="♀ (female rounded)"]
  XTAL2 = Crystal [frequency="16 Mhz" package=THT]
  C8 = Ceramic Capacitor [capacitance=22pF voltage=16V package="100 mil [THT, multilayer]"]
  C9 = Ceramic Capacitor [capacitance=22pF voltage=16V package="100 mil [THT, multilayer]"]

nets:
  N1: VDC_IN.V+, R11.Pin_0, U3.VCC, U3.AVCC, U3.AREF, BlueTooth_HC6.pin5
  N2: VDC_IN.V-, C8.1, C9.1
  N3: R9.Pin_0, R10.Pin_1, BlueTooth_HC6.pin2
  GND: R9.Pin_1, BlueTooth_HC6.pin4
  N4: R10.Pin_0, U3.D1_(TX)
  N5: R11.Pin_1, U3.RESET
  N6: U3.D0_(RX), BlueTooth_HC6.pin3
  N7: U3.XLAT1, XTAL2.pin_1, C9.0
  N8: U3.XLAT2, XTAL2.pin_0, C8.0
  N9: U3.D5_(PWM), Motor_Wheel_Signal_4.pin2
  N10: U3.D6_(PWM), Motor_Wheel_Signal_4.pin1
  N11: U3.D9_(PWM), Motor_Wheel_Signal_3.pin2
  N12: U3.D10_(PWM), Motor_Wheel_Signal_3.pin1
