# Fritzing sketch motors (saved by Fritzing 0.9.3b)
breadboards: 1

parts:
  VCC = Battery block 9V
  IC6 = L293D [package=THT]
  C3 = Electrolytic Capacitor [capacitance=10μF voltage=50V package="0605 [SMD, electrolytic]"]
  C4 = Electrolytic Capacitor [capacitance=10μF voltage=50V package="0605 [SMD, electrolytic]"]
  Motor_Wheel_3 = male pin header, 2 pins [form="♂ (male)"]
  D3 = Rectifier Diode [part_number=1N4001 package="300 mil [THT]"]
  D4 = Rectifier Diode [part_number=1N4001 package="300 mil [THT]"]
  Motor_2_In2 = male pin header, 2 pins [form="♂ (male)"]
  Motor_1_In1 = male pin header, 2 pins [form="♂ (male)"]
  5v_VDC_Out1 = male pin header, 2 pins [form="♂ (male)"]
  Motor_Wheel_4 = male pin header, 2 pins [form="♂ (male)"]
  U1 = Voltage Regulator - 5V [package="TO220 [THT]"]
  Switch = SPST Switch [package=switch-spdt-smd]
  R15 = Resistor [tolerance=±5% resistance=220 package="0402 [SMD]"]
  LED = smd LED [color="Green (570nm)" package="1206 [SMD]"]

nets:
  N1: VCC.-, C3.-, C4.-, 5v_VDC_Out1.pin2, U1.GND
  N2: VCC.+, D3.anode, Switch.P
  N3: IC6.Enable_1, IC6.Enable_2, IC6.+V, D4.cathode, 5v_VDC_Out1.pin1, R15.Pin_0
  N4: IC6.In_1, Motor_1_In1.pin1
  N5: IC6.Out_1_(_Controlled_by_Enable_1_), Motor_Wheel_4.pin1
  GND: IC6.0V, LED.cathode
  N6: IC6.Out_2_(_Controlled_by_Enable_1_), Motor_Wheel_4.pin2
  N7: IC6.In_2, Motor_1_In1.pin2
  N8: IC6.+Vmotor, D3.cathode
  N9: IC6.In_3, Motor_2_In2.pin2
  N10: IC6.Out_3_(_Controlled_by_Enable_2_), Motor_Wheel_3.pin2
  N11: IC6.Out_4_(_Controlled_by_Enable_2_), Motor_Wheel_3.pin1
  N12: IC6.In_4, Motor_2_In2.pin1
  N13: C3.+, U1.input_voltage, Switch.S
  N14: C4.+, D4.anode, U1.output_voltage
  N15: R15.Pin_1, LED.anode
